# Fritzing sketch ArduinoMini_Photogate_Transmitter (saved by Fritzing 0.9.3b)
stripboards: 1

parts:
  Part1 = Arduino Nano (Rev3.0)
  U2 = LCD-16X2 [package=lcd-16x2]
  J1 = Infrared Proximity Sensor
  R1 = Resistor [tolerance=±5% resistance=820 package="0805 [SMD]"]
  Part2 = NRF24L01+ Breakout Board

nets:
  GND: Part1.GND, U2.VSS, U2.R_W, U2.K, J1.GND, R1.Pin_0, Part2.GND
  N1: Part1.D2, U2.RS
  N2: Part1.D3, U2.E
  N3: Part1.D4, U2.DB4
  N4: Part1.D5, U2.DB5
  N5: Part1.D6, U2.DB6
  N6: Part1.D7, U2.DB7
  N7: Part1.D9, Part2.CE
  N8: Part1.D10, Part2.CS
  N9: Part1.D11/MOSI, Part2.MOSI
  N10: Part1.D12/MISO, Part2.MISO
  5V: Part1.5V, U2.VDD, U2.A, J1.Vcc
  N11: Part1.A6, J1.Vout
  3V3: Part1.3V3, Part2.VCC
  N12: Part1.D13/SCK, Part2.SCK
  N13: U2.VO, R1.Pin_1
